# Fritzing sketch ejemplo1 (saved by Fritzing 0.9.9b)
breadboards: 1

parts:
  Componente1 = Arduino Uno (Rev3)
  R1 = Resistor [tolerance=±5% power=0.25 resistance=220 package=THT]
  LED1 = LED - 5mm [color="Red (633nm)" current=0.030 package="5 mm [THT]"]

nets:
  N1: Componente1.D13/SCK, R1.Pin_0
  N2: Componente1.GND, LED1.cathode
  N3: R1.Pin_1, LED1.anode

// code stored in the sketch: ejemplo1.ino
/*

Autor: Learning Electronics with Arduino: An Illustrated Beginner's Guide to Physical Computing
Resumen: 
URL: https://github.com/arduinotogo/LEA/blob/master/LEA4_SOS.ino
*/

void setup() {
  // put your setup code here, to run once:
  pinMode(13, OUTPUT);
}

void loop() {
  // 3 short flashes
  digitalWrite(13, HIGH);//turn the LED on(HIGH is the voltage level)
  delay(500);            //wait for a half second
  digitalWrite(13, LOW); //turn the LED off by making the voltage LOW
  delay(300);      //pause for 300 milliseconds, about 1/3 of a second
  digitalWrite(13, HIGH);   
  delay(500);              
  digitalWrite(13, LOW);    
  delay(300); 
  digitalWrite(13, HIGH);   
  delay(500);              
  digitalWrite(13, LOW);    
  delay(300);   
  
   //three long flashes
  digitalWrite(13, HIGH);   //turn the LED on 
  delay(1500);              //wait for a second and a half
  digitalWrite(13, LOW); //turn the LED off by making the voltage LOW
  delay(300); 
  digitalWrite(13, HIGH);   
  delay(1500);             
  digitalWrite(13, LOW);   
  delay(300); 
  digitalWrite(13, HIGH);   
  delay(1500);             
  digitalWrite(13, LOW);    
  delay(300);   
    
   // 3 short flashes again
  digitalWrite(13, HIGH); //turn the LED on 
  delay(500);            //wait for a half second
  digitalWrite(13, LOW); //turn the LED off by making the voltage LOW
  delay(300); 
  digitalWrite(13, HIGH);   
  delay(500);              
  digitalWrite(13, LOW);    
  delay(300); 
  digitalWrite(13, HIGH);   
  delay(500);              
  digitalWrite(13, LOW);    
  delay(3000);         //final delay is 3 seconds
}
