# Fritzing sketch Ejemplo 2 (saved by Fritzing 0.9.9b)
breadboards: 1

parts:
  Esquema = Arduino Uno (Rev3)
  S1 = Pushbutton [package="[SMD]"]
  R1 = Resistor [tolerance=±5% power=0.25 resistance=10k package=THT]
  SP1 = SPEAKER [package=pcb_mount_speaker]
  R2 = Resistor [tolerance=±5% power=0.25 resistance=220 package=THT]
  LED1 = smd LED [color="Red (633nm)" package="1206 [SMD]"]

nets:
  N1: Esquema.D11_PWM/MOSI, SP1.-
  N2: Esquema.D13/SCK, R2.Pin_0
  N3: Esquema.GND, R1.Pin_0, SP1.+, LED1.cathode
  N4: Esquema.D2, S1.Pin_1, S1.Pin_2, R1.Pin_1
  N5: Esquema.5V, S1.Pin_3, S1.Pin_4
  N6: R2.Pin_1, LED1.anode
